# Fritzing sketch Bluetooth_Car (saved by Fritzing 1.0.5)
breadboards: 1

parts:
  Part1 = Arduino Uno (Rev3)
  M2 = DC Motor [voltage_(max)=6V voltage_(min)=3V]
  M3 = DC Motor [voltage_(max)=6V voltage_(min)=3V]
  M4 = DC Motor [voltage_(max)=6V voltage_(min)=3V]
  Part2 = Bluetooth HM-10
  M5 = DC Motor [voltage_(max)=6V voltage_(min)=3V]
  L298N1 = L298N DC motor driver
  VCC1 = 4 x AAA Battery Mount [internal_resistance=0.1Ω]
  SW1 = Slide_Switch_new

nets:
  GND: Part1.GND, Part2.GND, L298N1.GND, VCC1.-
  N1: Part1.D2, Part2.TXD
  N2: Part1.D3_PWM, Part2.RXD
  5V: Part1.5V, Part2.VCC, L298N1.12V, SW1.pin_1
  N3: M2.pin_1, M4.pin_1, L298N1.OUT3
  N4: M2.pin_2, M4.pin_2, L298N1.OUT4
  N5: M3.pin_1, M5.pin_1, L298N1.OUT2
  N6: M3.pin_2, M5.pin_2, L298N1.OUT1
  N7: VCC1.+, SW1.pin_2

custom parts:
  L298N DC motor driver: 2x DC motor driver with 78M05 positive voltage regulator (7..35 V) L298N: max 46 V, 2 A Set 5 V Enable jumper to enable 5 V regultor (needed for the L298N) and +5 V output at screw terminal or supply external +5 V at screw terminal Set ENA and/or ENB to +5 V to enable motor permanently or supply ENA and/or ENB with PWM signal IN1 and IN2 set rotation directory for motor A (OUT1/OUT2) IN2 and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
  Slide_Switch_new: the New two pin slide switch

// code stored in the sketch: Bluetooth_Car_Code.ino
#define CUSTOM_SETTINGS
#define INCLUDE_GAMEPAD_MODULE
#include <Dabble.h>

//Right motors
int rightMotorPin1=7;
int rightMotorPin2=8;

//Left motors
int leftMotorPin1=9;
int leftMotorPin2=10;

void setup()
{
  // put your setup code here, to run once:
  pinMode(rightMotorPin1,OUTPUT);
  pinMode(rightMotorPin2,OUTPUT);
  pinMode(leftMotorPin1,OUTPUT);
  pinMode(leftMotorPin2,OUTPUT);
  Dabble.begin(9600, 2, 3);
}



void loop()
{
  Dabble.processInput();
  
  if (GamePad.isUpPressed())
  {
    digitalWrite(rightMotorPin1,LOW);
    digitalWrite(rightMotorPin2,HIGH);  

    digitalWrite(leftMotorPin1,LOW);
    digitalWrite(leftMotorPin2,HIGH);     
  }

  else if (GamePad.isDownPressed())
  {
    digitalWrite(rightMotorPin1, HIGH);
    digitalWrite(rightMotorPin2, LOW);

    digitalWrite(leftMotorPin1, HIGH);
    digitalWrite(leftMotorPin2, LOW);  
  }

  else if (GamePad.isLeftPressed())
  {
     digitalWrite(rightMotorPin1, LOW);
     digitalWrite(rightMotorPin2, LOW);

    digitalWrite(leftMotorPin1, HIGH);
    digitalWrite(leftMotorPin2, LOW);
  }

  else if (GamePad.isRightPressed())
  {
    digitalWrite(rightMotorPin1, HIGH);
    digitalWrite(rightMotorPin2, LOW);  
  
    digitalWrite(leftMotorPin1, LOW);
    digitalWrite(leftMotorPin2, LOW);
  }
  else 
  {
     digitalWrite(rightMotorPin1, LOW);
      digitalWrite(rightMotorPin2, LOW);
    
      digitalWrite(leftMotorPin1, LOW);
      digitalWrite(leftMotorPin2, LOW);
  }
 
}

// code stored in the sketch: Bluetooth_Car_Code_TMP.ino
#define CUSTOM_SETTINGS
#define INCLUDE_GAMEPAD_MODULE
#include <Dabble.h>

//Right motors
int rightMotorPin1=7;
int rightMotorPin2=8;

//Left motors
int leftMotorPin1=9;
int leftMotorPin2=10;

void setup()
{
  // put your setup code here, to run once:
  pinMode(rightMotorPin1,OUTPUT);
  pinMode(rightMotorPin2,OUTPUT);
  pinMode(leftMotorPin1,OUTPUT);
  pinMode(leftMotorPin2,OUTPUT);
  Dabble.begin(9600, 2, 3);
}



void loop()
{
  Dabble.processInput();
  
  if (GamePad.isUpPressed())
  {
    digitalWrite(rightMotorPin1,LOW);
    digitalWrite(rightMotorPin2,HIGH);  

    digitalWrite(leftMotorPin1,LOW);
    digitalWrite(leftMotorPin2,HIGH);     
  }

  else if (GamePad.isDownPressed())
  {
    digitalWrite(rightMotorPin1, HIGH);
    digitalWrite(rightMotorPin2, LOW);

    digitalWrite(leftMotorPin1, HIGH);
    digitalWrite(leftMotorPin2, LOW);  
  }

  else if (GamePad.isLeftPressed())
  {
     digitalWrite(rightMotorPin1, LOW);
     digitalWrite(rightMotorPin2, LOW);

    digitalWrite(leftMotorPin1, HIGH);
    digitalWrite(leftMotorPin2, LOW);
  }

  else if (GamePad.isRightPressed())
  {
    digitalWrite(rightMotorPin1, HIGH);
    digitalWrite(rightMotorPin2, LOW);  
  
    digitalWrite(leftMotorPin1, LOW);
    digitalWrite(leftMotorPin2, LOW);
  }
  else 
  {
     digitalWrite(rightMotorPin1, LOW);
      digitalWrite(rightMotorPin2, LOW);
    
      digitalWrite(leftMotorPin1, LOW);
      digitalWrite(leftMotorPin2, LOW);
  }
 
}
